// Logisim project ALUstart.circ as structural Verilog: 1 circuit, main circuit main
module main (
  input  BInvert,
  input  AInvert,
  input  [3:0] A,
  input  [1:0] Operation,
  input  [6:0] in_5,
  input  in_6,
  input  in_7,
  input  [3:0] B,
  input  in_9,
  input  in_10,
  input  Less,
  input  Less_2,
  input  Less_3
);

  wire and_1_out, and_2_out, and_3_out, and_4_out, and_5_out, and_6_out, and_7_out, and_8_out, and_9_out,
       and_10_out, and_11_out, and_12_out, and_13_out, and_14_out, and_15_out, and_16_out, and_17_out,
       and_18_out, and_19_out, and_20_out, and_21_out, and_22_out, and_23_out, and_24_out, and_25_out,
       and_26_out, and_27_out, and_28_out, and_29_out, and_30_out, and_31_out, and_32_out, and_33_out,
       and_34_out, and_35_out, and_36_out, and_37_out, clock_1_out, multiplexer_1_out, multiplexer_2_out,
       multiplexer_3_out, multiplexer_4_out, multiplexer_5_out, multiplexer_6_out, multiplexer_7_out,
       multiplexer_8_out, not_1_out, not_2_out, not_3_out, not_4_out, not_5_out, not_6_out, not_7_out,
       not_8_out, not_9_out, not_10_out, not_11_out, not_12_out, not_13_out, not_14_out, not_15_out,
       not_16_out, not_17_out, not_18_out, not_19_out, not_20_out, not_21_out, or_1_out, or_2_out, or_3_out,
       or_4_out, or_5_out, or_6_out, or_7_out, or_8_out, or_9_out, or_10_out, or_11_out, or_12_out,
       or_13_out, or_14_out, or_15_out;
  wire [3:0] multiplexer_9_out, random_1_out, random_2_out;

  Clock clock_1 (.out(clock_1_out));
  Random #(.width(4)) random_1 (.clk(clock_1_out), .out(random_1_out));  // open: next, clr
  Random #(.width(4)) random_2 (.clk(clock_1_out), .out(random_2_out));  // open: next, clr
  Multiplexer multiplexer_1 (.in0(A[0]), .in1(not_1_out), .out(multiplexer_1_out), .sel(AInvert));  // open: en
  not not_1 (not_1_out, A[0]);
  not not_2 (not_2_out, B[0]);
  Multiplexer multiplexer_2 (.in0(A[1]), .in1(not_3_out), .out(multiplexer_2_out), .sel(AInvert));  // open: en
  not not_3 (not_3_out, A[1]);
  not not_4 (not_4_out, B[1]);
  Multiplexer multiplexer_3 (.in0(A[2]), .in1(not_5_out), .out(multiplexer_3_out), .sel(AInvert));  // open: en
  not not_5 (not_5_out, A[2]);
  not not_6 (not_6_out, B[2]);
  not not_7 (not_7_out, A[3]);
  Multiplexer multiplexer_4 (.in0(B[0]), .in1(not_2_out), .out(multiplexer_4_out), .sel(BInvert));  // open: en
  Multiplexer multiplexer_5 (.in0(B[1]), .in1(not_4_out), .out(multiplexer_5_out), .sel(BInvert));  // open: en
  Multiplexer multiplexer_6 (.in0(B[2]), .in1(not_6_out), .out(multiplexer_6_out), .sel(BInvert));  // open: en
  Multiplexer multiplexer_7 (.in0(A[3]), .in1(not_7_out), .out(multiplexer_7_out), .sel(AInvert));  // open: en
  Multiplexer multiplexer_8 (.in0(B[3]), .in1(not_8_out), .out(multiplexer_8_out), .sel(BInvert));  // open: en
  not not_8 (not_8_out, B[3]);
  not not_9 (not_9_out, BInvert);
  not not_10 (not_10_out, or_6_out);
  not not_11 (not_11_out, or_8_out);
  and and_1 (and_1_out, multiplexer_1_out, multiplexer_4_out);
  or or_1 (or_1_out, multiplexer_4_out, multiplexer_1_out);
  not not_12 (not_12_out, multiplexer_1_out);
  and and_2 (and_2_out, multiplexer_2_out, multiplexer_5_out);
  or or_2 (or_2_out, multiplexer_5_out, multiplexer_2_out);
  not not_13 (not_13_out, multiplexer_2_out);
  and and_3 (and_3_out, multiplexer_3_out, multiplexer_6_out);
  or or_3 (or_3_out, multiplexer_6_out, multiplexer_3_out);
  not not_14 (not_14_out, multiplexer_3_out);
  not not_15 (not_15_out, or_10_out);
  not not_16 (not_16_out, multiplexer_4_out);
  not not_17 (not_17_out, multiplexer_5_out);
  not not_18 (not_18_out, multiplexer_6_out);
  and and_4 (and_4_out, multiplexer_7_out, multiplexer_8_out);
  or or_4 (or_4_out, multiplexer_8_out, multiplexer_7_out);
  not not_19 (not_19_out, multiplexer_7_out);
  Multiplexer #(.select(2)) multiplexer_9 (
    .in0(and_1_out), .in1(or_1_out), .in2(or_5_out), .in3(or_11_out), .out(multiplexer_9_out[0]),
    .sel(Operation));  // open: en
  and and_5 (and_5_out, not_12_out, BInvert, not_16_out);
  and and_6 (and_6_out, not_12_out, not_9_out, multiplexer_4_out);
  and and_7 (and_7_out, multiplexer_1_out, not_16_out, not_9_out);
  and and_8 (and_8_out, multiplexer_4_out, multiplexer_1_out, BInvert);
  and and_9 (and_9_out, multiplexer_4_out, BInvert);
  and and_10 (and_10_out, multiplexer_1_out, BInvert);
  and and_11 (and_11_out, multiplexer_4_out, multiplexer_1_out);
  Multiplexer #(.select(2)) multiplexer_10 (
    .in0(and_2_out), .in1(or_2_out), .in2(or_7_out), .in3(Less), .out(multiplexer_9_out[1]), .sel(Operation));  // open: en
  and and_12 (and_12_out, not_13_out, or_6_out, not_17_out);
  and and_13 (and_13_out, not_13_out, not_10_out, multiplexer_5_out);
  and and_14 (and_14_out, multiplexer_2_out, not_17_out, not_10_out);
  and and_15 (and_15_out, multiplexer_5_out, multiplexer_2_out, or_6_out);
  and and_16 (and_16_out, multiplexer_5_out, or_6_out);
  and and_17 (and_17_out, multiplexer_2_out, or_6_out);
  and and_18 (and_18_out, multiplexer_5_out, multiplexer_2_out);
  Multiplexer #(.select(2)) multiplexer_11 (
    .in0(and_3_out), .in1(or_3_out), .in2(or_9_out), .in3(Less_2), .out(multiplexer_9_out[2]), .sel(Operation));  // open: en
  and and_19 (and_19_out, not_14_out, or_8_out, not_18_out);
  and and_20 (and_20_out, not_14_out, not_11_out, multiplexer_6_out);
  and and_21 (and_21_out, multiplexer_3_out, not_18_out, not_11_out);
  and and_22 (and_22_out, multiplexer_6_out, multiplexer_3_out, or_8_out);
  and and_23 (and_23_out, multiplexer_6_out, or_8_out);
  and and_24 (and_24_out, multiplexer_3_out, or_8_out);
  and and_25 (and_25_out, multiplexer_6_out, multiplexer_3_out);
  not not_20 (not_20_out, multiplexer_8_out);
  Multiplexer #(.select(2)) multiplexer_12 (
    .in0(and_4_out), .in1(or_4_out), .in2(or_11_out), .in3(Less_3), .out(multiplexer_9_out[3]),
    .sel(Operation));  // open: en
  and and_26 (and_26_out, not_19_out, or_10_out, not_20_out);
  and and_27 (and_27_out, not_19_out, not_15_out, multiplexer_8_out);
  and and_28 (and_28_out, multiplexer_7_out, not_20_out, not_15_out);
  and and_29 (and_29_out, multiplexer_8_out, multiplexer_7_out, or_10_out);
  and and_30 (and_30_out, multiplexer_8_out, or_10_out);
  and and_31 (and_31_out, multiplexer_7_out, or_10_out);
  and and_32 (and_32_out, multiplexer_8_out, multiplexer_7_out);
  or or_5 (or_5_out, and_5_out, and_6_out, and_7_out, and_8_out);
  or or_6 (or_6_out, and_9_out, and_10_out, and_11_out);
  or or_7 (or_7_out, and_12_out, and_13_out, and_14_out, and_15_out);
  or or_8 (or_8_out, and_16_out, and_17_out, and_18_out);
  or or_9 (or_9_out, and_19_out, and_20_out, and_21_out, and_22_out);
  or or_10 (or_10_out, and_23_out, and_24_out, and_25_out);
  or or_11 (or_11_out, and_26_out, and_27_out, and_28_out, and_29_out);
  or or_12 (or_12_out, and_30_out, and_31_out, and_32_out);
  and and_33 (and_33_out, ~A[3], ~B[3]);  // AND_Gate
  and and_34 (and_34_out, A[3], B[3]);
  or or_13 (or_13_out, and_33_out, and_34_out);
  or or_14 (or_14_out, or_5_out, or_7_out, or_9_out, or_11_out);
  TTY #(.trigger("falling")) tty_1 (
    .data({in_10, in_9, in_6, multiplexer_9_out}), .clk(clock_1_out), .clr(in_7));  // open: we
  not not_21 (not_21_out, or_14_out);
  and and_35 (and_35_out, or_11_out, and_33_out);
  and and_36 (and_36_out, ~Operation[0], Operation[1], or_13_out, ~BInvert, or_12_out);  // AND_Gate
  and and_37 (and_37_out, ~Operation[0], Operation[1], or_12_out, ~or_13_out, BInvert);  // AND_Gate
  LED Equals (.in(not_21_out));
  or or_15 (or_15_out, and_35_out, and_36_out, and_37_out);
  LED Overflow (.in(or_15_out));
endmodule
